// Logisim project cpu.circ as structural Verilog: 5 circuits, main circuit main
module main (
  input  [31:0] in_1
);

  wire AddI, And, Beq, bitfinder_1_found, bitfinder_2_found, Jump, Load, Mult, not_1_out, Or, Resta, Store,
       Suma, Tipo_R;
  wire [3:0] bit_extender_1_out, bit_extender_2_out, bit_extender_3_out, controlled_buffer_2_out,
       controlled_buffer_2_out_2;
  wire [4:0] controlled_buffer_1_out, Rd, Rs, Rt;
  wire [7:0] A, B, C, D;
  wire [15:0] Address;
  wire [15:8] controlled_buffer_2_out_3;
  wire [25:0] JAddress;

  Multiplexer #(.width(8), .disabled(0), .enable("false")) multiplexer_1 (
    .in1(8'h5f), .out(A), .sel(Suma));  // open: in0
  Multiplexer #(.width(8), .disabled(0), .enable("false")) multiplexer_2 (
    .in1(8'h6e), .out(A), .sel(Resta));  // open: in0
  Multiplexer #(.width(8), .disabled(0), .enable("false")) multiplexer_3 (
    .in1(8'h5f), .out(A), .sel(And));  // open: in0
  Multiplexer #(.width(8), .disabled(0), .enable("false")) multiplexer_4 (.in1(8'h77), .out(A), .sel(Or));  // open: in0
  Multiplexer #(.width(8), .disabled(0), .enable("false")) multiplexer_5 (
    .in1(8'h5a), .out(A), .sel(Mult));  // open: in0
  Multiplexer #(.width(8), .disabled(0), .enable("false")) multiplexer_6 (
    .in1(8'h7c), .out(A), .sel(Beq));  // open: in0
  Multiplexer #(.width(8), .disabled(0), .enable("false")) multiplexer_7 (
    .in1(8'h5f), .out(A), .sel(AddI));  // open: in0
  Multiplexer #(.width(8), .disabled(0), .enable("false")) multiplexer_8 (
    .in1(8'h34), .out(A), .sel(Load));  // open: in0
  Multiplexer #(.width(8), .disabled(0), .enable("false")) multiplexer_9 (
    .in1(8'h6e), .out(A), .sel(Store));  // open: in0
  Multiplexer #(.width(8), .disabled(0), .enable("false")) multiplexer_10 (
    .in1(8'h61), .out(A), .sel(Jump));  // open: in0
  decoder decoder_1 (
    .Address(Address), .in_1(in_1), .Tipo_R(Tipo_R), .Rd(Rd), .Rt(Rt), .Rs(Rs), .out_7(JAddress),
    .Suma(Suma), .Resta(Resta), .And(And), .Or(Or), .Mult(Mult), .Beq(Beq), .AddI(AddI), .Load(Load),
    .Store(Store), .Jump(Jump));
  Multiplexer #(.width(8), .disabled(0), .enable("false")) multiplexer_11 (
    .in1(8'h79), .out(B), .sel(Suma));  // open: in0
  Multiplexer #(.width(8), .disabled(0), .enable("false")) multiplexer_12 (
    .in1(8'h75), .out(B), .sel(Resta));  // open: in0
  Multiplexer #(.width(8), .disabled(0), .enable("false")) multiplexer_13 (
    .in1(8'h57), .out(B), .sel(And));  // open: in0
  Multiplexer #(.width(8), .disabled(0), .enable("false")) multiplexer_14 (
    .in1(8'h16), .out(B), .sel(Or));  // open: in0
  Multiplexer #(.width(8), .disabled(0), .enable("false")) multiplexer_15 (
    .in1(8'h75), .out(B), .sel(Mult));  // open: in0
  Multiplexer #(.width(8), .disabled(0), .enable("false")) multiplexer_16 (
    .in1(8'h3f), .out(B), .sel(Beq));  // open: in0
  Multiplexer #(.width(8), .disabled(0), .enable("false")) multiplexer_17 (
    .in1(8'h79), .out(B), .sel(AddI));  // open: in0
  Multiplexer #(.width(8), .disabled(0), .enable("false")) multiplexer_18 (
    .in1(8'h77), .out(B), .sel(Load));  // open: in0
  Multiplexer #(.width(8), .disabled(0), .enable("false")) multiplexer_19 (
    .in1(8'h3c), .out(B), .sel(Store));  // open: in0
  Multiplexer #(.width(8), .disabled(0), .enable("false")) multiplexer_20 (
    .in1(8'h75), .out(B), .sel(Jump));  // open: in0
  Multiplexer #(.width(8), .disabled(0), .enable("false")) multiplexer_21 (
    .in1(8'h79), .out(C), .sel(Suma));  // open: in0
  Multiplexer #(.width(8), .disabled(0), .enable("false")) multiplexer_22 (
    .in1(8'h7c), .out(C), .sel(Resta));  // open: in0
  Multiplexer #(.width(8), .disabled(0), .enable("false")) multiplexer_23 (
    .in1(8'h79), .out(C), .sel(And));  // open: in0
  Multiplexer #(.width(8), .disabled(0), .enable("false")) multiplexer_24 (
    .in1(8'h34), .out(C), .sel(Mult));  // open: in0
  Multiplexer #(.width(8), .disabled(0), .enable("false")) multiplexer_25 (
    .in1(8'h4f), .out(C), .sel(Beq));  // open: in0
  Multiplexer #(.width(8), .disabled(0), .enable("false")) multiplexer_26 (
    .in1(8'h79), .out(C), .sel(AddI));  // open: in0
  Multiplexer #(.width(8), .disabled(0), .enable("false")) multiplexer_27 (
    .in1(8'h5f), .out(C), .sel(Load));  // open: in0
  Multiplexer #(.width(8), .disabled(0), .enable("false")) multiplexer_28 (
    .in1(8'h5a), .out(C), .sel(Jump));  // open: in0
  _7_Segment_Display u_7_segment_display_1 (
    .g(A[3]), .f(A[2]), .a(A[1]), .b(A[0]), .e(A[4]), .d(A[5]), .c(A[6]));  // open: dp
  Multiplexer #(.width(8), .disabled(0), .enable("false")) multiplexer_29 (
    .in1(8'h14), .out(D), .sel(AddI));  // open: in0
  Multiplexer #(.width(8), .disabled(0), .enable("false")) multiplexer_30 (
    .in1(8'h79), .out(D), .sel(Load));  // open: in0
  Multiplexer #(.width(8), .disabled(0), .enable("false")) multiplexer_31 (
    .in1(8'h3c), .out(D), .sel(Mult));  // open: in0
  Multiplexer #(.width(8), .disabled(0), .enable("false")) multiplexer_32 (
    .in1(8'h1f), .out(D), .sel(Jump));  // open: in0
  _7_Segment_Display u_7_segment_display_2 (
    .g(B[3]), .f(B[2]), .a(B[1]), .b(B[0]), .e(B[4]), .d(B[5]), .c(B[6]));  // open: dp
  _7_Segment_Display u_7_segment_display_3 (
    .g(C[3]), .f(C[2]), .a(C[1]), .b(C[0]), .e(C[4]), .d(C[5]), .c(C[6]));  // open: dp
  _7_Segment_Display u_7_segment_display_4 (
    .g(D[3]), .f(D[2]), .a(D[1]), .b(D[0]), .e(D[4]), .d(D[5]), .c(D[6]));  // open: dp
  Hex_Digit_Display hex_digit_display_1 (.value(Rs[3:0]));  // open: dp
  Hex_Digit_Display hex_digit_display_2 (.value(bit_extender_1_out));  // open: dp
  assign bit_extender_1_out = {{3{1'b0}}, Rs[4]};  // Bit_Extender bit_extender_1
  Hex_Digit_Display hex_digit_display_3 (.value(controlled_buffer_2_out_3[15:12]));  // open: dp
  Hex_Digit_Display hex_digit_display_4 (.value(bit_extender_2_out));  // open: dp
  assign bit_extender_2_out = {{3{1'b0}}, Rt[4]};  // Bit_Extender bit_extender_2
  Hex_Digit_Display hex_digit_display_5 (.value(controlled_buffer_2_out_3[11:8]));  // open: dp
  Hex_Digit_Display hex_digit_display_6 (.value(Rt[3:0]));  // open: dp
  assign controlled_buffer_1_out = bitfinder_2_found ? Rd : 5'bz;  // Controlled_Buffer controlled_buffer_1
  Hex_Digit_Display hex_digit_display_7 (.value(controlled_buffer_2_out));  // open: dp
  Hex_Digit_Display hex_digit_display_8 (.value(controlled_buffer_2_out_2));  // open: dp
  assign {controlled_buffer_2_out_3, controlled_buffer_2_out_2, controlled_buffer_2_out} = bitfinder_1_found ? Address : 16'bz;  // Controlled_Buffer controlled_buffer_2
  Hex_Digit_Display hex_digit_display_9 (.value(controlled_buffer_1_out[3:0]));  // open: dp
  Hex_Digit_Display hex_digit_display_10 (.value(bit_extender_3_out));  // open: dp
  assign bit_extender_3_out = {{3{1'b0}}, controlled_buffer_1_out[4]};  // Bit_Extender bit_extender_3
  BitFinder #(.width(1)) bitfinder_1 (.in(not_1_out), .found(bitfinder_1_found));  // open: index
  not not_1 (not_1_out, Tipo_R);
  BitFinder #(.width(1)) bitfinder_2 (.in(Tipo_R), .found(bitfinder_2_found));  // open: index

  // Notes on the sheet:
  //   Decoder
  //   Instruction
  //   rs
  //   rt
  //   Address
  //   rd
endmodule

module decoder (
  input  [31:0] in_1,
  output Tipo_R,
  output [15:0] Address,
  output [4:0] Rd,
  output [4:0] Rt,
  output [4:0] Rs,
  output [25:0] out_7,
  output Suma,
  output Resta,
  output And,
  output Or,
  output Mult,
  output Beq,
  output AddI,
  output Load,
  output Store,
  output Jump
);

  wire comparator_1_eq, comparator_2_eq, comparator_3_eq, comparator_4_eq, comparator_5_eq, comparator_7_eq,
       comparator_8_eq, comparator_9_eq, comparator_10_eq, comparator_11_eq, not_1_out, not_2_out, not_3_out,
       not_4_out, not_5_out;

  Comparator #(.width(6)) comparator_1 (.a(in_1[5:0]), .b(6'b100000), .eq(comparator_1_eq));  // open: gt, lt
  not not_1 (not_1_out, Tipo_R);
  Comparator #(.width(6)) comparator_2 (.a(in_1[31:26]), .b(6'b000100), .eq(comparator_2_eq));  // open: gt, lt
  not not_2 (not_2_out, Tipo_R);
  Comparator #(.width(6)) comparator_3 (.a(in_1[31:26]), .b(6'b000010), .eq(comparator_3_eq));  // open: gt, lt
  and and_1 (Suma, Tipo_R, comparator_1_eq);
  and and_2 (Beq, not_1_out, comparator_2_eq);
  and and_3 (Jump, not_2_out, comparator_3_eq);
  Comparator #(.width(6)) comparator_4 (.a(in_1[5:0]), .b(6'b100010), .eq(comparator_4_eq));  // open: gt, lt
  Comparator #(.width(6)) comparator_5 (.a(in_1[31:26]), .b(6'b001000), .eq(comparator_5_eq));  // open: gt, lt
  and and_4 (Resta, Tipo_R, comparator_4_eq);
  not not_3 (not_3_out, Tipo_R);
  and and_5 (AddI, not_3_out, comparator_5_eq);
  Comparator #(.width(6)) comparator_6 (.a(in_1[31:26]), .b({6{1'b0}}), .eq(Tipo_R));  // open: gt, lt
  Comparator #(.width(6)) comparator_7 (.a(in_1[5:0]), .b(6'b100100), .eq(comparator_7_eq));  // open: gt, lt
  and and_6 (And, Tipo_R, comparator_7_eq);
  not not_4 (not_4_out, Tipo_R);
  Comparator #(.width(6)) comparator_8 (.a(in_1[31:26]), .b(6'b100011), .eq(comparator_8_eq));  // open: gt, lt
  and and_7 (Load, not_4_out, comparator_8_eq);
  Comparator #(.width(6)) comparator_9 (.a(in_1[5:0]), .b(6'b100101), .eq(comparator_9_eq));  // open: gt, lt
  Comparator #(.width(6)) comparator_10 (.a(in_1[31:26]), .b(6'b101011), .eq(comparator_10_eq));  // open: gt, lt
  and and_8 (Or, Tipo_R, comparator_9_eq);
  not not_5 (not_5_out, Tipo_R);
  and and_9 (Store, not_5_out, comparator_10_eq);
  Comparator #(.width(6)) comparator_11 (.a(in_1[5:0]), .b(6'b011000), .eq(comparator_11_eq));  // open: gt, lt
  and and_10 (Mult, Tipo_R, comparator_11_eq);

  assign Address = in_1[15:0];
  assign out_7 = in_1[25:0];
  assign Rd = in_1[15:11];
  assign Rs = in_1[25:21];
  assign Rt = in_1[20:16];

  // Other names for the same wires on the sheet: Funct[5:0] = in_1[5:0]; OpCode[5:0] = in_1[31:26]
endmodule

module pc (
  input  clk,
  output [31:0] data
);

  wire [7:0] register_1_q_2;
  wire [23:0] register_1_q;
  wire [31:0] adder_1_out;

  Register #(.width(32)) register_1 (.D(adder_1_out), .Q({register_1_q_2, register_1_q}), .clk(clk));  // open: en, clr
  Adder #(.width(32)) adder_1 (.a(32'h1), .b({register_1_q_2, register_1_q}), .out(adder_1_out));  // open: cin, cout
  ROM rom_1 (.pos(register_1_q), .data(data));  // open: sel
endmodule

module RAM (
  input  [23:0] pos,
  input  [31:0] data,
  input  sel,
  input  clk,
  input  ld,
  input  clr
);

  RAM_part #(.addrWidth(24), .dataWidth(32)) ram_1 (.addr(pos), .data(data), .sel(sel), .clk(clk), .ld(ld), .clr(clr));
endmodule

module ROM (
  input  [23:0] pos,
  input  sel,
  output [31:0] data
);

  ROM_part #(.addrWidth(24), .dataWidth(32)) rom_1 (.addr(pos), .data(data), .sel(sel));
endmodule
